# Fritzing sketch circuitDiagram (saved by Fritzing 0.8.5b)
breadboards: 1

parts:
  Part1 = Arduino Uno (Rev3)  # not connected
  Part2 = Rotoshield - Motor driver shield for Arduino
  R1 = Resistor [tolerance=±5% resistance=10k package=THT]
  J1 = Basic Servo  # not connected
  S1 = Momentary Switch [package=ksa_sealed_tac_switch]
  S2 = Momentary Switch [package=ksa_sealed_tac_switch]  # not connected
  M1 = Stepper Motor - Bipolar
  M2 = Stepper Motor - Unipolar
  V1 = DC Power [voltage=12V]  # not connected

nets:
  N1: Part2.M1-2, M1.B
  N2: Part2.M1-1, M1.D
  N3: Part2.M2-2, M1.A
  N4: Part2.M2-1, M1.C
  N5: Part2.GND, M2.C
  N6: Part2.2, R1.Pin_0, S1.4
  GND: R1.Pin_1
